// Logisim project adder4.circ as structural Verilog: 4 circuits, main circuit implementation
module implementation (
  input  [3:0] Ain,
  input  [3:0] Bin,
  input  Cinin,
  output [3:0] Sum_Out,
  output Carry_Out
);

  wire and_4_out, and_5_out, C0, C1, C2, E2, E3, E4, E5, G0, G1, G2, G3, P0, P1, P2, P3;

  G u_G3 (.in_1(Ain[3]), .in_2(Bin[3]), .out_3(G3));
  P u_P3 (.in_1(Ain[3]), .in_2(Bin[3]), .out_3(P3));
  G u_G2 (.in_1(Ain[2]), .in_2(Bin[2]), .out_3(G2));
  P u_P2 (.in_1(Ain[2]), .in_2(Bin[2]), .out_3(P2));
  G u_G1 (.in_1(Ain[1]), .in_2(Bin[1]), .out_3(G1));
  G u_G0 (.in_1(Ain[0]), .in_2(Bin[0]), .out_3(G0));
  P u_P1 (.in_1(Ain[1]), .in_2(Bin[1]), .out_3(P1));
  P u_P0 (.in_1(Ain[0]), .in_2(Bin[0]), .out_3(P0));
  and and_1 (E2, P3, G2);
  and and_2 (E3, P3, P2, G1);
  and and_3 (E4, P3, P2, P1, G0);
  and and_4 (and_4_out, P0, Cinin);
  // OR_Gate or_1 has open pins: in0=G1, in1=and_5_out, out=open
  and and_5 (and_5_out, P1, G0);
  and and_6 (E5, P3, P2, P1, P0, Cinin);
  or or_2 (C0, G0, and_4_out);
  or or_3 (Carry_Out, G3, E2, E3, E4, E5);
  Sum1 sum1_1 (.in_1(Ain[3]), .in_2(Bin[3]), .in_3(C2), .out_4(Sum_Out[3]));
  Sum1 sum1_2 (.in_1(Ain[2]), .in_2(Bin[2]), .in_3(C1), .out_4(Sum_Out[2]));
  Sum1 sum1_3 (.in_1(Ain[1]), .in_2(Bin[1]), .in_3(C0), .out_4(Sum_Out[1]));
  Sum1 sum1_4 (.in_1(Ain[0]), .in_2(Bin[0]), .in_3(Cinin), .out_4(Sum_Out[0]));

  // Other names for the same wires on the sheet: A[3:0] = Ain; A0 = Ain[0]; A1 = Ain[1]; A2 = Ain[2]; A3 = Ain[3];
  //   B[3:0] = Bin; B0 = Bin[0]; B1 = Bin[1]; B2 = Bin[2]; B3 = Bin[3]; C3 = Carry_Out; Cin = Cinin;
  //   Sum[3:0] = Sum_Out
endmodule

module G (
  input  in_1,
  input  in_2,
  output out_3
);

  and and_1 (out_3, in_1, in_2);
endmodule

module P (
  input  in_1,
  input  in_2,
  output out_3
);

  xor xor_1 (out_3, in_1, in_2);
endmodule

module Sum1 (
  input  in_1,
  input  in_2,
  input  in_3,
  output out_4
);

  ExactlyOne xor_1 (.out(out_4), .in0(in_1), .in1(in_2), .in2(in_3));
endmodule
